# Fritzing sketch PNP_NPN_fader-a--r00a2 (saved by Fritzing 0.9.3b)
breadboards: 1

parts:
  Q1 = PNP-Transistor [package="TO92 [THT]"]
  LED1 = LED - 5mm [color="Red (633nm)" package="5 mm [THT]"]
  R1 = Resistor [tolerance=±5% resistance=33 package=THT]
  VCC1 = Battery
  R2 = Rotary Potentiometer (Small) [maximum_resistance=100kΩ package=THT]
  R3 = Resistor [tolerance=±5% resistance=180k package=THT]

nets (from the breadboard view):
  N1: Q1.E, VCC1.+, R2.leg1
  N2: Q1.B, R3.Pin_1
  N3: Q1.C, LED1.anode
  N4: LED1.cathode, R1.Pin_0
  N5: R1.Pin_1, VCC1.-, R2.leg2
  N6: R2.wiper, R3.Pin_0
