# Fritzing sketch PNP_following_NPN-r00b (saved by Fritzing 0.9.0b)
breadboards: 1

parts:
  Q1 = NPN-Transistor [package="TO92 [THT]"]
  Q2 = PNP-Transistor [package="TO92 [THT]"]
  LED1 = LED - 5mm [color="Red (633nm)" package="5 mm [THT]"]
  R2 = Resistor [tolerance=±5% resistance=1k package=THT]
  R1 = Resistor [tolerance=±5% resistance=47k package=THT]
  R3 = Resistor [tolerance=±5% resistance=1k package=THT]
  R4 = Resistor [tolerance=±5% resistance=2.2k package=THT]
  Part2 = Adafruit Feather M0 Express [part_number="Adafruit #3403"]

nets:
  N1: Q1.E, R4.Pin_1, Part2.GND
  N2: Q1.B, R1.Pin_1
  N3: Q1.C, R2.Pin_0
  N4: Q2.E, R3.Pin_1, Part2.+3V3
  N5: Q2.B, R2.Pin_1, R3.Pin_0
  N6: Q2.C, LED1.anode
  N7: LED1.cathode, R4.Pin_0
  N8: R1.Pin_0, Part2.D6

custom parts:
  Adafruit Feather M0 Express: We love all our Feathers equally, but this Feather is very special. It's our first Feather that is specifically designed for use with CircuitPython! CircuitPython is our beginner-oriented flavor of MicroPython - and as the name hints at, its a small but full-featured version of the popular Python programming language specifically for use with circuitry and electronics. That doesn't mean you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
