# Fritzing sketch PNP_following_NPN-r00c2 (saved by Fritzing 0.9.0b)
breadboards: 1

parts:
  Q1 = NPN-Transistor [package="TO92 [THT]"]
  Q2 = PNP-Transistor [package="TO92 [THT]"]
  LED1 = LED - 5mm [color="Red (633nm)" package="5 mm [THT]"]
  R2 = Resistor [tolerance=±5% resistance=1k package=THT]
  R1 = Resistor [tolerance=±5% resistance=47k package=THT]
  R3 = Resistor [tolerance=±5% resistance=1k package=THT]
  R4 = Resistor [tolerance=±5% resistance=2.2k package=THT]
  Part2 = Adafruit Feather M0 Express [part_number="Adafruit #3403"]
  Q3 = ULN2803 Darlington Array

nets:
  GND: Q1.E, Part2.GND, Q3.GND
  N1: Q1.B, R1.Pin_1
  N2: Q1.C, R2.Pin_0
  N3: Q2.E, R3.Pin_1, Part2.+3V3, Q3.COMMON
  N4: Q2.B, R2.Pin_1, R3.Pin_0
  N5: Q2.C, LED1.anode
  N6: LED1.cathode, R4.Pin_0
  N7: R1.Pin_0, Part2.D12
  N8: R4.Pin_1, Q3.O1
  N9: Part2.D6, Q3.I1

custom parts:
  Adafruit Feather M0 Express: We love all our Feathers equally, but this Feather is very special. It's our first Feather that is specifically designed for use with CircuitPython! CircuitPython is our beginner-oriented flavor of MicroPython - and as the name hints at, its a small but full-featured version of the popular Python programming language specifically for use with circuitry and electronics. That doesn't mean you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
  ULN2803 Darlington Array: ULN2803 Darlington Transistor Array with Flyback Protection
