# Fritzing sketch Two_Micros_TX_RX_UART--r01-a (saved by Fritzing 0.9.0b)
breadboards: 1

parts:
  D2 = Rectifier Diode [part_number=1N4148 package="300 mil [THT]"]
  D3 = Rectifier Diode [part_number=1N4148 package="300 mil [THT]"]
  D4 = Rectifier Diode [part_number=1N4148 package="300 mil [THT]"]
  D5 = Rectifier Diode [part_number=1N4148 package="300 mil [THT]"]
  D6 = Rectifier Diode [part_number=1N4148 package="300 mil [THT]"]
  D7 = Rectifier Diode [part_number=1N4148 package="300 mil [THT]"]
  D8 = Rectifier Diode [part_number=1N4148 package="300 mil [THT]"]
  Part1 = Adafruit Feather M0 Basic Proto [part_number="Adafruit #2772"]
  Part2 = Adafruit Feather M0 Basic Proto [part_number="Adafruit #2772"]
  D1 = Rectifier Diode [part_number=1N4148 breakdown_voltage=3.6V package="300 mil [THT]"]

nets:
  N1: D2.cathode, D4.cathode, Part2.+3V3
  N2: D2.anode, D5.cathode, D6.anode, Part1.D0, Part2.D1, D1.cathode
  N3: D3.cathode, D4.anode, D7.cathode, D8.anode, Part1.D1, Part2.D0
  GND: D3.anode, D5.anode, D7.anode, Part1.GND, Part2.GND, D1.anode
  N4: D6.cathode, D8.cathode, Part1.+3V3

custom parts:
  Adafruit Feather M0 Basic Proto: At the Feather M0's heart is an ATSAMD21G18 ARM Cortex M0 processor, clocked at 48 MHz and at 3.3V logic, the same one used in the new Arduino Zero. This chip has a whopping 256K of FLASH (8x more than the Atmega328 or 32u4) and 32K of RAM (16x as much)! This chip comes with built in USB so it has USB-to-Serial program & debug capability built in with no need for an FTDI-like chip. To make it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
